# Fritzing sketch RFID_Reader (saved by Fritzing 0.9.3b)
circuit board: 8.46667cm x 5.64444cm

parts:
  Bauteil1 = RFID-RC522-v2
  WeMos_D1_Mini1 = WeMos D1 Mini
  SG2 = Buzzer 12mm [package=buzzer-12mm-ns]
  S1 = Momentary Switch [package=ksa_sealed_tac_switch]
  LED1 = smd LED [color="Red (633nm)" package="1206 [SMD]"]
  R1 = Resistor [tolerance=±5% resistance=1k package="0805 [SMD]"]
  HLK-PM1 = HLK-PM01

nets:
  N1: Bauteil1.SDA, WeMos_D1_Mini1.D8
  N2: Bauteil1.SCK, WeMos_D1_Mini1.D5
  N3: Bauteil1.MOSI, WeMos_D1_Mini1.D7
  N4: Bauteil1.MISO, WeMos_D1_Mini1.D6
  N5: Bauteil1.GND, WeMos_D1_Mini1.G, S1.4, HLK-PM1.-Vo
  N6: Bauteil1.RST, WeMos_D1_Mini1.D3
  3.3V: Bauteil1.3.3V, WeMos_D1_Mini1.3V3
  N7: WeMos_D1_Mini1.5V, SG2.1, R1.Pin_1, HLK-PM1.+Vo
  N8: WeMos_D1_Mini1.D0, SG2.2
  N9: WeMos_D1_Mini1.D2, S1.2
  N10: WeMos_D1_Mini1.D4, LED1.cathode
  N11: LED1.anode, R1.Pin_0

custom parts:
  RFID-RC522-v2: A simple China made RFID-RC522 Reader; do check the pin labels, as this is a MFRC522 based clone.
