# Fritzing sketch RFID_Reader_RDM6300 (saved by Fritzing 0.9.3b)
circuit board: 8.46667cm x 5.64444cm

parts:
  WeMos_D1_Mini1 = WeMos D1 Mini
  SG2 = Buzzer 12mm [package=buzzer-12mm-ns]
  S1 = Momentary Switch [package=ksa_sealed_tac_switch]
  LED1 = smd LED [color="Red (633nm)" package="1206 [SMD]"]
  R1 = Resistor [tolerance=±5% resistance=1k package="0805 [SMD]"]
  125_kHz_RFID_module1 = RDM6300

nets:
  5V: WeMos_D1_Mini1.5V, R1.Pin_1, 125_kHz_RFID_module1.+5V
  N1: WeMos_D1_Mini1.D1, SG2.1
  N2: WeMos_D1_Mini1.D2, S1.2
  N3: WeMos_D1_Mini1.D4, LED1.cathode
  N4: WeMos_D1_Mini1.G, SG2.2, S1.4, 125_kHz_RFID_module1.NULL, 125_kHz_RFID_module1.GND#60
  N5: WeMos_D1_Mini1.RX, 125_kHz_RFID_module1.TX, 125_kHz_RFID_module1.GND#66
  N6: LED1.anode, R1.Pin_0

custom parts:
  RDM6300: 125 kHz RFID module (serial interface)
